# Fritzing sketch adc_read (saved by Fritzing 0.8.5b)
breadboards: 1

parts:
  Arduino_UNO_R3 = Arduino Uno (Rev3)
  R5 = Resistor [tolerance=±5% resistance=1k package=THT]
  LED1 = LED - 5mm [color="Red (633nm)" package="5 mm [THT]"]
  R6 = Rotary Potentiometer (Small) [maximum_resistance=100kΩ package=THT]

nets:
  N1: Arduino_UNO_R3.A0, R6.wiper
  N2: Arduino_UNO_R3.D9_PWM, R5.Pin_1
  N3: Arduino_UNO_R3.GND, LED1.cathode, R6.leg1
  N4: Arduino_UNO_R3.5V, R6.leg2
  N5: R5.Pin_0, LED1.anode
