# Fritzing sketch adc_volt (saved by Fritzing 0.8.5b)
breadboards: 1

parts:
  Arduino_UNO_R3 = Arduino Uno (Rev3)
  R5 = Resistor [tolerance=±5% resistance=1k package=THT]
  LED1 = LED - 5mm [color="Red (633nm)" package="5 mm [THT]"]

nets:
  N1: Arduino_UNO_R3.A0, Arduino_UNO_R3.5V
  N2: Arduino_UNO_R3.D9_PWM, R5.Pin_1
  N3: Arduino_UNO_R3.GND, LED1.cathode
  N4: R5.Pin_0, LED1.anode
