# Fritzing sketch bluetooth (saved by Fritzing 0.8.5b)
breadboards: 1

parts:
  Arduino_UNO_R3 = Arduino Uno (Rev3)
  R5 = Resistor [tolerance=±5% resistance=1k package=THT]
  LED1 = LED - 5mm [color="Red (633nm)" package="5 mm [THT]"]
  Bluetooth = China Sensors [part_number=Sensors]

nets:
  N1: Arduino_UNO_R3.D9_PWM, R5.Pin_1
  GND: Arduino_UNO_R3.GND, Bluetooth.GND
  N2: Arduino_UNO_R3.D2, Arduino_UNO_R3.D3_PWM, Bluetooth.RXD, Bluetooth.TXD
  3V3: Arduino_UNO_R3.3V3, Bluetooth.VCC
  N3: R5.Pin_0, LED1.anode

custom parts:
  China Sensors: Plug-in Network Module having W5200 & Mag Jack
