# Fritzing sketch buzzer (saved by Fritzing 0.8.5b)
breadboards: 1

parts:
  Arduino_UNO_R3 = Arduino Uno (Rev3)
  R5 = Resistor [tolerance=±5% resistance=1k package=THT]
  J1 = Piezo Speaker
  Q1 = NPN-Transistor [package="TO92 [THT]"]

nets:
  N1: Arduino_UNO_R3.D8, R5.Pin_1
  N2: Arduino_UNO_R3.GND, J1.pin1
  N3: Arduino_UNO_R3.5V, Q1.E
  N4: R5.Pin_0, Q1.B
  N5: J1.pin2, Q1.C
