# Fritzing sketch buzzer_base (saved by Fritzing 0.8.5b)
breadboards: 1

parts:
  Arduino_UNO_R3 = Arduino Uno (Rev3)
  Buzzer = Piezo Speaker

nets:
  N1: Arduino_UNO_R3.D8, Buzzer.pin2
  N2: Arduino_UNO_R3.GND, Buzzer.pin1
