# Fritzing sketch cds (saved by Fritzing 0.8.5b)
breadboards: 1

parts:
  Arduino_UNO_R3 = Arduino Uno (Rev3)
  R5 = Resistor [tolerance=±5% resistance=1k package=THT]
  LED1 = LED - 5mm [color="Red (633nm)" package="5 mm [THT]"]
  R6 = Resistor [tolerance=±5% resistance=10k package=THT]
  R7 = Photocell (LDR) [package=THT]

nets:
  N1: Arduino_UNO_R3.A0, R6.Pin_1, R7.pin_1
  N2: Arduino_UNO_R3.D11_PWM/MOSI, R5.Pin_1
  N3: Arduino_UNO_R3.GND, LED1.cathode, R6.Pin_0
  N4: Arduino_UNO_R3.5V, R7.pin_0
  N5: R5.Pin_0, LED1.anode
