# Fritzing sketch dc_motor (saved by Fritzing 0.8.5b)
breadboards: 1

parts:
  Arduino_UNO_R3 = Arduino Uno (Rev3)
  IC1 = L293D [package=THT]
  M1 = DC Motor
  D1 = Rectifier Diode [part_number=1N4001 package="300 mil [THT]"]
  D2 = Rectifier Diode [part_number=1N4001 package="300 mil [THT]"]

nets:
  N1: Arduino_UNO_R3.D9_PWM, IC1.Enable_1
  N2: Arduino_UNO_R3.GND, IC1.0V
  N3: Arduino_UNO_R3.D2, IC1.In_1
  N4: Arduino_UNO_R3.D4, IC1.In_2
  N5: Arduino_UNO_R3.5V, IC1.+Vmotor, IC1.+V, D1.cathode, D2.cathode
  N6: IC1.Out_1_(_Controlled_by_Enable_1_), M1.pin_2, D1.anode
  N7: M1.pin_1, D2.anode
