# Fritzing sketch dht11 (saved by Fritzing 0.8.5b)
breadboards: 1

parts:
  Arduino_UNO_R3 = Arduino Uno (Rev3)
  RHT1 = Humidity and Temperature Sensor RHT03
  R1 = Resistor [tolerance=±5% resistance=4.7k package=THT]

nets:
  N1: Arduino_UNO_R3.GND, RHT1.GND_2
  N2: Arduino_UNO_R3.D2, RHT1.Data-signal, R1.Pin_0
  5V: Arduino_UNO_R3.5V, RHT1.Vcc, R1.Pin_1
