# Fritzing sketch fire_sensor (saved by Fritzing 0.8.5b)
breadboards: 1

parts:
  Arduino_UNO_R3 = Arduino Uno (Rev3)
  LED2 = LED - 5mm [color="Yellow (595nm)" package="5 mm [THT]"]
  R7 = Resistor [tolerance=±5% resistance=1k package=THT]
  Fire_Sensor = China Sensors [part_number=Sensors]

nets:
  GND: Arduino_UNO_R3.GND, Arduino_UNO_R3.D2, R7.Pin_0, Fire_Sensor.DO, Fire_Sensor.GND
  N1: Arduino_UNO_R3.D3_PWM, LED2.anode
  5V: Arduino_UNO_R3.5V, Fire_Sensor.VCC
  N2: LED2.cathode, R7.Pin_1

custom parts:
  China Sensors: Plug-in Network Module having W5200 & Mag Jack
