# Fritzing sketch fnd - 복사본 (saved by Fritzing 0.8.5b)
breadboards: 1

parts:
  Arduino_UNO_R3 = Arduino Uno (Rev3)
  7_Segment1 = 7 Segment Display
  R1 = Resistor [tolerance=±5% resistance=470 package=THT]
  R2 = Resistor [tolerance=±5% resistance=470 package=THT]
  R3 = Resistor [tolerance=±5% resistance=470 package=THT]
  R4 = Resistor [tolerance=±5% resistance=470 package=THT]
  R5 = Resistor [tolerance=±5% resistance=470 package=THT]
  R6 = Resistor [tolerance=±5% resistance=470 package=THT]
  R7 = Resistor [tolerance=±5% resistance=470 package=THT]
  R8 = Resistor [tolerance=±5% resistance=470 package=THT]

nets:
  N1: Arduino_UNO_R3.D8, 7_Segment1.Segment_B, R2.Pin_0, R2.Pin_1
  N2: Arduino_UNO_R3.D9_PWM, 7_Segment1.Segment_A, R1.Pin_0, R1.Pin_1
  N3: Arduino_UNO_R3.GND, 7_Segment1.common_anode
  N4: Arduino_UNO_R3.D2, 7_Segment1.Segment_G, R5.Pin_0, R5.Pin_1
  N5: Arduino_UNO_R3.D3_PWM, 7_Segment1.Segment_F, R6.Pin_0, R6.Pin_1
  N6: Arduino_UNO_R3.D4, 7_Segment1.Segment_E, R7.Pin_0, R7.Pin_1
  N7: Arduino_UNO_R3.D5_PWM, 7_Segment1.Segment_D, R8.Pin_0, R8.Pin_1
  N8: Arduino_UNO_R3.D6_PWM, 7_Segment1.Segment_DP, R4.Pin_0, R4.Pin_1
  N9: Arduino_UNO_R3.D7, 7_Segment1.Segment_C, R3.Pin_0, R3.Pin_1
