# Fritzing sketch gyro_servo (saved by Fritzing 0.8.5b)
breadboards: 1

parts:
  Arduino_UNO_R3 = Arduino Uno (Rev3)
  L3G4200D1 = L3G4200D [package=THT]
  J2 = Basic Servo

nets:
  N1: Arduino_UNO_R3.D8, J2.pulse
  N2: Arduino_UNO_R3.D10_PWM/SS, L3G4200D1.CS
  N3: Arduino_UNO_R3.D11_PWM/MOSI, L3G4200D1.SDA
  VCC: Arduino_UNO_R3.D12/MISO, Arduino_UNO_R3.3V3, L3G4200D1.VCC, L3G4200D1.SDO, J2.vcc
  N4: Arduino_UNO_R3.D13/SCK, L3G4200D1.SCL
  GND: Arduino_UNO_R3.GND, L3G4200D1.GND, J2.gnd
  N5: Arduino_UNO_R3.D6_PWM, L3G4200D1.DR
  N6: Arduino_UNO_R3.D7, L3G4200D1.INT
