# Fritzing sketch hc_sr04 (saved by Fritzing 0.8.5b)
breadboards: 1

parts:
  Arduino_UNO_R3 = Arduino Uno (Rev3)
  part = HC-SR04 [part_number=HC-SR04]

nets:
  GND: Arduino_UNO_R3.D12/MISO, Arduino_UNO_R3.GND, part.GND, part.ECHO
  N1: Arduino_UNO_R3.D13/SCK, part.TRIG
  5V: Arduino_UNO_R3.5V, part.VCC
