# Fritzing sketch ir_receiver (saved by Fritzing 0.8.5b)
breadboards: 1

parts:
  Arduino_UNO_R3 = Arduino Uno (Rev3)
  LM35/CH0B = CH0B IRDA Receiver [package="TO92 [THT]"]
  R1 = Resistor [tolerance=±5% resistance=220 package=THT]
  LED1 = LED - 5mm [color="Red (633nm)" package="5 mm [THT]"]

nets:
  N1: Arduino_UNO_R3.D12/MISO, R1.Pin_1, LED1.anode
  GND: Arduino_UNO_R3.GND, LM35/CH0B.GND, R1.Pin_0, LED1.cathode
  N2: Arduino_UNO_R3.D2, LM35/CH0B.Output
  5V: Arduino_UNO_R3.5V, LM35/CH0B.VCC

custom parts:
  CH0B IRDA Receiver: CH0B IRDA Receiver.
