# Fritzing sketch ir_sender (saved by Fritzing 0.8.5b)
breadboards: 1

parts:
  Arduino_UNO_R3 = Arduino Uno (Rev3)
  LED1 = LED - 5mm [color="Infrared (940nm)" package="5 mm [THT]"]
  Q1 = NPN-Transistor [package="TO92 [THT]"]
  R1 = Resistor [tolerance=±5% resistance=100 package=THT]
  R2 = Resistor [tolerance=±5% resistance=470 package=THT]

nets:
  N1: Arduino_UNO_R3.GND, R1.Pin_1
  N2: Arduino_UNO_R3.D3_PWM, Q1.B, R2.Pin_0, R2.Pin_1
  N3: Arduino_UNO_R3.5V, LED1.anode
  N4: LED1.cathode, Q1.C
  N5: Q1.E, R1.Pin_0
