# Fritzing sketch key1 (saved by Fritzing 0.8.5b)
breadboards: 1

parts:
  Arduino_UNO_R3 = Arduino Uno (Rev3)
  R5 = Resistor [tolerance=±5% resistance=1k package=THT]
  R6 = Resistor [tolerance=±5% resistance=10k package=THT]
  LED1 = LED - 5mm [color="Blue (525nm)" package="5 mm [THT]"]
  LED2 = LED - 5mm [color="Yellow (595nm)" package="5 mm [THT]"]
  R7 = Resistor [tolerance=±5% resistance=1k package=THT]
  S1 = Pushbutton [package="[THT]"]
  S2 = Pushbutton [package="[THT]"]
  R8 = Resistor [tolerance=±5% resistance=10k package=THT]

nets:
  N1: Arduino_UNO_R3.GND, R5.Pin_0, R6.Pin_0, R7.Pin_0, R8.Pin_0
  N2: Arduino_UNO_R3.5V, R6.Pin_1, LED1.anode, LED2.anode, S1.Pin_1, S1.Pin_2, S1.Pin_3, S1.Pin_4, S2.Pin_1, S2.Pin_2, S2.Pin_3, S2.Pin_4, R8.Pin_1
  N3: R5.Pin_1, LED1.cathode
  N4: LED2.cathode, R7.Pin_1
