# Fritzing sketch l3g4200_i2c (saved by Fritzing 0.8.5b)
breadboards: 1

parts:
  Arduino_UNO_R3 = Arduino Uno (Rev3)
  L3G4200D1 = L3G4200D [package=THT]

nets:
  N1: Arduino_UNO_R3.A4/SDA, L3G4200D1.SDA
  N2: Arduino_UNO_R3.A5/SCL, L3G4200D1.SCL
  GND: Arduino_UNO_R3.GND, L3G4200D1.GND
  3V3: Arduino_UNO_R3.3V3, L3G4200D1.VCC, L3G4200D1.SDO
