# Fritzing sketch l3g4200_spi (saved by Fritzing 0.8.5b)
breadboards: 1

parts:
  Arduino_UNO_R3 = Arduino Uno (Rev3)
  L3G4200D1 = L3G4200D [package=THT]

nets:
  N1: Arduino_UNO_R3.D10_PWM/SS, L3G4200D1.CS
  N2: Arduino_UNO_R3.D11_PWM/MOSI, L3G4200D1.SDA
  3V3: Arduino_UNO_R3.D12/MISO, Arduino_UNO_R3.3V3, L3G4200D1.VCC, L3G4200D1.SDO
  N3: Arduino_UNO_R3.D13/SCK, L3G4200D1.SCL
  GND: Arduino_UNO_R3.GND, L3G4200D1.GND
  N4: Arduino_UNO_R3.D6_PWM, L3G4200D1.DR
  N5: Arduino_UNO_R3.D7, L3G4200D1.INT
