# Fritzing sketch lcd_parallel_8bit (saved by Fritzing 0.8.5b)
breadboards: 1

parts:
  Arduino_UNO_R3 = Arduino Uno (Rev3)
  LCD1 = LCD screen
  R1 = Trimmer Potentiometer [maximum_resistance=10kΩ package=THT]

nets (from the breadboard view):
  N1: Arduino_UNO_R3.D8, LCD1.DB5
  N2: Arduino_UNO_R3.D9_PWM, LCD1.DB6
  N3: Arduino_UNO_R3.D10_PWM/SS, LCD1.DB7
  N4: Arduino_UNO_R3.D11_PWM/MOSI, LCD1.R/W
  N5: Arduino_UNO_R3.D12/MISO, LCD1.RS
  GND: Arduino_UNO_R3.GND, LCD1.VSS, R1.leg2
  N6: Arduino_UNO_R3.D2, LCD1.E
  N7: Arduino_UNO_R3.D3_PWM, LCD1.DB0
  N8: Arduino_UNO_R3.D4, LCD1.DB1
  N9: Arduino_UNO_R3.D5_PWM, LCD1.DB2
  N10: Arduino_UNO_R3.D6_PWM, LCD1.DB3
  N11: Arduino_UNO_R3.D7, LCD1.DB4
  5V: Arduino_UNO_R3.5V, LCD1.VDD, R1.leg1
  N12: LCD1.V0, R1.wiper
