# Fritzing sketch lcd_serial (saved by Fritzing 0.8.5b)

parts:
  Arduino_UNO_R3 = Arduino Uno (Rev3)
  IC1 = LCD1602 Serial [package=THT]

nets:
  GND: Arduino_UNO_R3.GND, IC1.GND
  N1: Arduino_UNO_R3.D1/TX, IC1.Rx
  5V: Arduino_UNO_R3.5V, IC1.VCC

custom parts:
  LCD1602 Serial: LCD1602 Serial by Robotbase
