# Fritzing sketch led (saved by Fritzing 0.8.5b)
breadboards: 1

parts:
  Arduino_UNO_R3 = Arduino Uno (Rev3)
  LED2 = LED - 5mm [color="Red (633nm)" package="5 mm [THT]"]
  R1 = Resistor [tolerance=±5% resistance=1k package=THT]
  R2 = Resistor [tolerance=±5% resistance=1k package=THT]
  LED1 = LED - 5mm [color="Red (633nm)" package="5 mm [THT]"]

nets:
  N1: Arduino_UNO_R3.D8, R2.Pin_0, R2.Pin_1, LED1.anode
  N2: Arduino_UNO_R3.D9_PWM, LED2.anode, R1.Pin_0, R1.Pin_1
  N3: Arduino_UNO_R3.GND, LED2.cathode, LED1.cathode
