# Fritzing sketch rs232_2 (saved by Fritzing 0.8.5b)
breadboards: 1

parts:
  Arduino_UNO_R3 = Arduino Uno (Rev3)
  R5 = Resistor [tolerance=±5% resistance=1k package=THT]
  LED1 = LED - 5mm [color="Blue (525nm)" package="5 mm [THT]"]
  LED2 = LED - 5mm [color="Yellow (595nm)" package="5 mm [THT]"]
  R7 = Resistor [tolerance=±5% resistance=1k package=THT]

nets:
  N1: Arduino_UNO_R3.GND, R5.Pin_0, R7.Pin_0
  N2: Arduino_UNO_R3.D6_PWM, LED1.anode
  N3: Arduino_UNO_R3.D7, LED2.anode
  N4: R5.Pin_1, LED1.cathode
  N5: LED2.cathode, R7.Pin_1
