# Fritzing sketch servo_motor (saved by Fritzing 0.8.5b)
breadboards: 1

parts:
  Arduino_UNO_R3 = Arduino Uno (Rev3)
  J1 = Basic Servo

nets:
  N1: Arduino_UNO_R3.D8, J1.pulse
  GND: Arduino_UNO_R3.GND, J1.gnd
  5V: Arduino_UNO_R3.5V, J1.vcc
