# Fritzing sketch step_motor (saved by Fritzing 0.8.5b)
breadboards: 1

parts:
  Arduino_UNO_R3 = Arduino Uno (Rev3)
  IC1 = L293D [package=THT]
  M1 = Stepper Motor - Unipolar

nets:
  N1: Arduino_UNO_R3.D8, IC1.In_1
  N2: Arduino_UNO_R3.D9_PWM, IC1.In_2
  N3: Arduino_UNO_R3.D10_PWM/SS, IC1.In_3
  N4: Arduino_UNO_R3.D11_PWM/MOSI, IC1.In_4
  N5: Arduino_UNO_R3.GND, IC1.0V
  N6: Arduino_UNO_R3.3V3, IC1.+Vmotor
  N7: Arduino_UNO_R3.5V, IC1.Enable_1, IC1.+V
  N8: IC1.Out_1_(_Controlled_by_Enable_1_), M1.C
  N9: IC1.Out_2_(_Controlled_by_Enable_1_), M1.A
  N10: IC1.Out_3_(_Controlled_by_Enable_2_), M1.D
  N11: IC1.Out_4_(_Controlled_by_Enable_2_), M1.B
