# Fritzing sketch web_server (saved by Fritzing 0.8.5b)
breadboards: 1

parts:
  Arduino_UNO_R3 = Arduino Uno (Rev3)
  LED2 = LED - 5mm [color="Red (633nm)" package="5 mm [THT]"]
  R6 = Resistor [tolerance=±5% resistance=1k package=THT]

nets:
  N1: Arduino_UNO_R3.GND, LED2.cathode, LED2.anode, R6.Pin_0
  N2: Arduino_UNO_R3.D3_PWM, R6.Pin_1
